# Fritzing sketch SenorCircuit_v1 (saved by Fritzing 0.9.0b)

parts:
  パーツ1 = LilyPad Accelerometer ADXL335
  パーツ3 = Bluetooth Mate Silver
  パーツ5 = Lilypad Battery Connect
  U1 = LIPO-2000mAh [package=lipo-2000]
  パーツ6 = Lilypad Arduino Board

nets:
  GND: パーツ1.COM, パーツ3.GND, パーツ5.-, U1.-, パーツ6.GND
  N1: パーツ1.XOUT, パーツ6.A0
  N2: パーツ1.YOUT, パーツ6.A1
  N3: パーツ1.ZOUT, パーツ6.A2
  5V: パーツ1.5V, パーツ3.CTS_5V, パーツ5.+, U1.+, パーツ6.VCC
  N4: パーツ3.TX_5V, パーツ6.D3
  N5: パーツ3.VCC, パーツ6.D2
