# Fritzing sketch SenorCircuit_v2 (saved by Fritzing 0.9.0b)
perfboards: 1

parts:
  パーツ5 = Lilypad Battery Connect
  U1 = LIPO-2000mAh [package=lipo-2000]
  パーツ6 = Lilypad Arduino Board
  パーツ3 = Bluetooth Mate Silver
  R1 = Resistor [tolerance=±5% resistance=1M package=THT]

nets:
  GND: パーツ5.-, U1.-, パーツ6.GND, パーツ3.GND
  N1: パーツ5.+, U1.+, パーツ6.VCC, パーツ3.CTS_5V
  N2: パーツ6.MISO/D12, R1.Pin_1
  N3: パーツ6.D3, パーツ3.TX_5V
  N4: パーツ6.D2, パーツ3.VCC
